// Logisim project BlackJack.circ as structural Verilog
module main (
  input  in_1,
  input  in_2,
  input  in_3,
  input  in_4,
  input  in_5,
  input  in_6,
  input  in_7,
  input  in_8,
  input  in_9,
  input  in_10,
  output [5:0] out_11,
  output out_12,
  output [5:0] out_13,
  output out_14,
  output [5:0] out_15,
  output out_16,
  output [5:0] out_17,
  output out_18,
  output [1:0] out_19,
  output [5:0] out_20,
  output out_21,
  output out_22,
  output out_23,
  output out_24,
  output out_25,
  output out_26,
  output out_27,
  output [5:0] out_28,
  output out_29,
  output [5:0] out_30,
  output out_31,
  output out_32,
  output out_33,
  output [5:0] out_34,
  output [5:0] out_35,
  output [5:0] out_36,
  output out_37,
  output [6:0] out_38,
  output [6:0] out_39,
  output out_40,
  output out_41,
  output out_42,
  output out_43
);

  wire and_gate_1_output, clock_1_out, demux1to2_1_i0, demux1to2_1_i1, or_gate_1_output, or_gate_2_output,
       or_gate_3_output, or_gate_4_output, or_gate_5_output, or_gate_6_output, or_gate_7_output,
       uc_1_demux_sel_p1, uc_1_demux_sel_p2, uc_1_draw_p1, uc_1_draw_p2, uc_1_enable_clk, uc_1_reset_state,
       uc_1_restart_state, xor_gate_1_output;
  wire [5:0] and_gate_6bits_1_output;
  wire [6:0] bcdto7_left_draw_1_output, bcdto7_right_draw_1_output, bcdto7right_1_output,
       bcdto7right_2_output;

  BCDto7LEFT bcdto7left_1 (.A(out_20), .\output (out_38));
  BcdTo7RIGHT bcdto7right_1 (.A(out_20), .\output (bcdto7right_1_output));
  Clock clock_1 (.out(clock_1_out));
  or_gate or_gate_1 (.A(out_12), .B(uc_1_reset_state), .\output (or_gate_1_output));
  and_gate_6bits and_gate_6bits_1 (.A(out_17), .B(or_gate_2_output), .\output (and_gate_6bits_1_output));
  ScoreCounter scorecounter_1 (.CLK(out_25), .RESET(or_gate_1_output), .\output (out_35));
  _7_Segment_Display u_7_segment_display_1 (
    .g(out_38[0]), .f(out_38[1]), .a(out_38[6]), .b(out_38[5]), .e(out_38[2]), .d(out_38[3]), .c(out_38[4]));  // open: dp
  _7_Segment_Display u_7_segment_display_2 (
    .g(bcdto7right_1_output[0]), .f(bcdto7right_1_output[1]), .a(bcdto7right_1_output[6]),
    .b(bcdto7right_1_output[5]), .e(bcdto7right_1_output[2]), .d(bcdto7right_1_output[3]),
    .c(bcdto7right_1_output[4]));  // open: dp
  bcdto7_left_draw bcdto7_left_draw_1 (.A(and_gate_6bits_1_output), .\output (bcdto7_left_draw_1_output));
  UC uc_1 (
    .START(in_1), .CLK(clock_1_out), .RESET(in_2), .restart(in_3), .end_game(in_4), .P1_READY(in_5),
    .P2_READY(in_6), .check_win(or_gate_7_output), .check_bust(or_gate_6_output), .p1_cardvalue(out_20),
    .p2_cardvalue(out_30), .P1_HIT(in_7), .P1_STAND(in_8), .P2_HIT(in_9), .P2_STAND(in_10),
    .idle_led(out_12), .P1_READY_LED(out_14), .P2_READY_LED(out_16), .game_started(out_18),
    .enable_clk(uc_1_enable_clk), .demux_sel_p1(uc_1_demux_sel_p1), .demux_sel_p2(uc_1_demux_sel_p2),
    .draw_p1(uc_1_draw_p1), .draw_p2(uc_1_draw_p2), .DRAW_LED(out_24), .P1_WIN(out_25), .P2_WIN(out_26),
    .reset_state(uc_1_reset_state), .restart_state(uc_1_restart_state), .end_game_state(out_27));
  _7_Segment_Display u_7_segment_display_3 (
    .g(bcdto7_left_draw_1_output[0]), .f(bcdto7_left_draw_1_output[1]), .a(bcdto7_left_draw_1_output[6]),
    .b(bcdto7_left_draw_1_output[5]), .e(bcdto7_left_draw_1_output[2]), .d(bcdto7_left_draw_1_output[3]),
    .c(bcdto7_left_draw_1_output[4]));  // open: dp
  bcdto7_right_draw bcdto7_right_draw_1 (.A(and_gate_6bits_1_output), .\output (bcdto7_right_draw_1_output));
  BCDto7LEFT bcdto7left_2 (.A(out_30), .\output (out_39));
  BcdTo7RIGHT bcdto7right_2 (.A(out_30), .\output (bcdto7right_2_output));
  _7_Segment_Display u_7_segment_display_4 (
    .g(bcdto7_right_draw_1_output[0]), .f(bcdto7_right_draw_1_output[1]), .a(bcdto7_right_draw_1_output[6]),
    .b(bcdto7_right_draw_1_output[5]), .e(bcdto7_right_draw_1_output[2]), .d(bcdto7_right_draw_1_output[3]),
    .c(bcdto7_right_draw_1_output[4]));  // open: dp
  and_gate and_gate_1 (.A(clock_1_out), .B(uc_1_enable_clk), .\output (and_gate_1_output));
  or_gate or_gate_2 (.A(and_gate_1_output), .B(xor_gate_1_output), .\output (or_gate_2_output));
  or_gate or_gate_3 (.A(out_12), .B(uc_1_reset_state), .\output (or_gate_3_output));
  or_gate or_gate_4 (.A(uc_1_demux_sel_p1), .B(uc_1_demux_sel_p2), .\output (or_gate_4_output));
  xor_gate xor_gate_1 (.A(uc_1_draw_p1), .B(uc_1_draw_p2), .\output (xor_gate_1_output));
  _7_Segment_Display u_7_segment_display_5 (
    .g(out_39[0]), .f(out_39[1]), .a(out_39[6]), .b(out_39[5]), .e(out_39[2]), .d(out_39[3]), .c(out_39[4]));  // open: dp
  FisherYates2 fisheryates2_1 (
    .clk(or_gate_2_output), .reset(or_gate_3_output), .card_out(out_11), .index_out(out_13),
    .output_signal_test(out_15));
  demux1to2 demux1to2_1 (
    .data_in(or_gate_2_output), .Select_data(or_gate_4_output), .I0(demux1to2_1_i0), .I1(demux1to2_1_i1));
  or_gate or_gate_5 (.A(or_gate_3_output), .B(uc_1_restart_state), .\output (or_gate_5_output));
  ScoreCounter scorecounter_2 (.CLK(out_26), .RESET(or_gate_1_output), .\output (out_34));
  _7_Segment_Display u_7_segment_display_6 (
    .g(bcdto7right_2_output[0]), .f(bcdto7right_2_output[1]), .a(bcdto7right_2_output[6]),
    .b(bcdto7right_2_output[5]), .e(bcdto7right_2_output[2]), .d(bcdto7right_2_output[3]),
    .c(bcdto7right_2_output[4]));  // open: dp
  SuitLed suitled_1 (
    .A(out_19), .enable(or_gate_2_output), .Hearts(out_40), .Diamonds(out_41), .Clubs(out_42), .Spades(out_43));
  CardValueP1Register cardvaluep1register_1 (
    .CLK(demux1to2_1_i0), .RESET(or_gate_5_output), .value_in(out_28), .value_out(out_20));
  AdderP1 adderp1_1 (.A(out_20), .B(out_17), .RESET(or_gate_5_output), .sum(out_28), .cout(out_29));
  CardValueP2Register cardvaluep2register_1 (
    .CLK(demux1to2_1_i1), .RESET(or_gate_5_output), .value_in(out_36), .value_out(out_30));
  DecoderCardValue decodercardvalue_1 (
    .value_in(out_11), .RESET(or_gate_5_output), .value_out(out_17), .suit_out(out_19));
  AdderP2 adderp2_1 (.A(out_30), .B(out_17), .RESET(or_gate_5_output), .sum(out_36), .cout(out_37));
  ComparatorP1 comparatorp1_1 (.A(out_20), .Over21(out_21), .Under21(out_22), .Is21(out_23));
  ComparatorP2 comparatorp2_1 (.A(out_30), .Over21(out_31), .Under21(out_32), .Is21(out_33));
  or_gate or_gate_6 (.A(out_21), .B(out_31), .\output (or_gate_6_output));
  or_gate or_gate_7 (.A(out_23), .B(out_33), .\output (or_gate_7_output));
endmodule

// VHDL entity FisherYates2, as the project stores it:
--------------------------------------------------------------------------------
-- Project :
-- File    :
-- Autor   :
-- Date    :
--
--------------------------------------------------------------------------------
-- Description :
--fiecare numar din array corespunde cu o carte, iar la fiecare extragere cartea se interschimba cu output_signal 
--astfel dupa fiecare parcurgere sirul va fi complet diferit fata de tura trecuta 
--------------------------------------------------------------------------------

LIBRARY ieee;
USE ieee.std_logic_1164.all;
use ieee.std_logic_unsigned.all;
use ieee.numeric_std.all;

ENTITY FisherYates2 IS
  PORT (clk: in std_logic;
  	   reset: in std_logic;
  	   card_out: out std_logic_vector(5 downto 0);
  	   index_out :out std_logic_vector(5 downto 0);
  	   output_signal_test: out std_logic_vector(5 downto 0)

    );
END FisherYates2;



architecture behavioural of FisherYates2 is
type card_array is array (0 to 51) of std_logic_vector(5 downto 0);
signal deck: card_array := (	"011101", "001111", "000101", "101001", "011010", "011110",
						"100010", "011000", "010010", "100110", "000110", "101111",
						"110100", "100001", "001001", "100111", "010100", "000111",
						"010011", "101010", "101110", "011011", "001010", "110001",
						"110101", "100011", "010111", "011001", "101000", "001011",
						"010000", "000001", "001100", "110011", "100101", "101100",
						"000011", "110010", "101101", "001110", "011100", "101011",
						"110110", "001101", "010110", "000010", "011111", "010101",
						"100000", "100100", "101010", "110000"
);

signal current_index : std_logic_vector(5 downto 0) := "000000";
signal temp : std_logic_vector(5 downto 0):= "000000";
signal output_signal : std_logic_vector(5 downto 0) := "000000";


BEGIN


	
	process(clk,reset )
	begin

		if(reset = '1') then 
			current_index <= "000000";
			deck <= (   	"011101", "001111", "000101", "101001", "011010", "011110",
						"100010", "011000", "010010", "100110", "000110", "101111",
						"110100", "100001", "001001", "100111", "010100", "000111",
						"010011", "101010", "101110", "011011", "001010", "110001",
						"110101", "100011", "010111", "011001", "101000", "001011",
						"010000", "000001", "001100", "110011", "100101", "101100",
						"000011", "110010", "101101", "001110", "011100", "101011",
						"110110", "001101", "010110", "000010", "011111", "010101",
						"100000", "100100", "101010", "110000"

				    );
			
		elsif(rising_edge(clk)) then
		
			if(current_index = "110011") then 
				current_index <= "000000";
			else 
				temp <= deck(to_integer(unsigned(current_index)));
				deck(to_integer(unsigned(current_index))) <= deck(to_integer(unsigned(output_signal)));
				deck(to_integer(unsigned(output_signal))) <= temp;
				current_index <= current_index + 1;

			end if;
			output_signal <= deck(to_integer(unsigned(current_index)) mod 3);
		end if;
	card_out <= deck(to_integer(unsigned(current_index)));
	index_out <= current_index;
	output_signal_test <= output_signal;
	
	end process;


END behavioural;

// VHDL entity CardValueP1Register, as the project stores it:
--------------------------------------------------------------------------------
-- Project :
-- File    :
-- Autor   :
-- Date    :
--
--------------------------------------------------------------------------------
-- Description :
--
--------------------------------------------------------------------------------

LIBRARY ieee;
USE ieee.std_logic_1164.all;

ENTITY CardValueP1Register IS
  PORT (CLK: in std_logic;
  	   RESET: in std_logic;
  	   value_in : in std_logic_vector(5 downto 0);
  	   value_out: out std_logic_vector(5 downto 0)
    );
END CardValueP1Register;

--------------------------------------------------------------------------------
--Complete your VHDL description below
--------------------------------------------------------------------------------

ARCHITECTURE TypeArchitecture OF CardValueP1Register IS
signal output : std_logic_vector(5 downto 0) := "000000";


BEGIN
	process(CLK, RESET)
	begin	
		if RESET = '1' then 
			output <= "000000";
		elsif rising_edge(CLK) then 
			output <= value_in;
		end if;

	value_out <= output;
	end process;

END TypeArchitecture;

// VHDL entity AdderP1, as the project stores it:
--------------------------------------------------------------------------------
-- Project :
-- File    :
-- Autor   :
-- Date    :
--
--------------------------------------------------------------------------------
-- Description :
--
--------------------------------------------------------------------------------

LIBRARY ieee;
USE ieee.std_logic_1164.all;
use ieee.numeric_std.all;
use ieee.std_logic_unsigned.all;


ENTITY AdderP1 IS
  port(A: in std_logic_vector(5 downto 0);
  	  B: in std_logic_vector(5 downto 0);
  	  RESET: in std_logic;

  	  sum: out std_logic_vector(5 downto 0);
  	  cout: out std_logic
    );
END AdderP1;

architecture arh1 of AdderP1 is
  signal output : std_logic_vector(5 downto 0) := "000000";
  signal carryOut : std_logic := '0';

begin
  process(A, B, RESET)
    variable carry : std_logic := '0';
    variable sum : std_logic_vector(5 downto 0) := "000000";
  begin
    if RESET = '1' then
      carry := '0';
      sum := (others => '0');
    else
      for i in 0 to 5 loop
        sum(i) := A(i) xor B(i) xor carry;
        carry := (A(i) and B(i)) or (carry and (A(i) xor B(i)));
      end loop;
    end if;

    output <= sum;
    carryOut <= carry;
  end process;
  
  sum <= output;
  cout <= carryOut;
  
end arh1;

// VHDL entity HeartsAdder, as the project stores it:
--------------------------------------------------------------------------------
-- Project :
-- File    :
-- Autor   :
-- Date    :
--
--------------------------------------------------------------------------------
-- Description :
--
--------------------------------------------------------------------------------

LIBRARY ieee;
USE ieee.std_logic_1164.all;
use ieee.std_logic_unsigned.all;
use ieee.numeric_std.all;

ENTITY HeartsAdder IS
  PORT (CLK: in std_logic;
  	   data_in : in std_logic_vector(2 downto 0);
  	   data_out : out std_logic_vector(2 downto 0);
  	   RESET: in std_logic;

  	   reached_max: out std_logic
    );
END HeartsAdder;

--------------------------------------------------------------------------------
--Complete your VHDL description below
--------------------------------------------------------------------------------

ARCHITECTURE TypeArchitecture OF HeartsAdder IS
signal count : std_logic_vector(2 downto 0) := "000";
signal max: std_logic := '0';


BEGIN
	process(CLK, RESET)
	begin
		if RESET = '1' then 
			max <= '0';
			count <= "000";
		elsif rising_edge(CLK) then 
			if count = "011" then
				max <= '1';
			else 
				max <= '0';
				count <= count + 1;
			end if;
		end if;

	end process;
	data_out <= count;
	reached_max <= max;


END TypeArchitecture;

// VHDL entity FisherYatesSUIT, as the project stores it:
--------------------------------------------------------------------------------
-- Project :
-- File    :
-- Autor   :
-- Date    :
--
--------------------------------------------------------------------------------
-- Description :
--

--------------------------------------------------------------------------------

LIBRARY ieee;
USE ieee.std_logic_1164.all;
use ieee.std_logic_unsigned.all;
use ieee.numeric_std.all;

ENTITY FisherYatesSUIT IS
  PORT (
clk: in std_logic;
  	   reset: in std_logic;
  	   card_out: out std_logic_vector(2 downto 0);
  	   index_out :out std_logic_vector(3 downto 0);
  	   output_signal_test: out std_logic_vector(2 downto 0)

    );
END FisherYatesSUIT;



architecture behavioural of FisherYatesSUIT is
type card_array is array (0 to 15) of std_logic_vector(2 downto 0);
signal deck: card_array := ("100", "001", "011", "010", "100", "010", "011", "001", "001", "011", "100", "010", "011", "001", 
						"010", "100"	);

signal current_index : std_logic_vector(3 downto 0) := "0000";
signal temp : std_logic_vector(2 downto 0):= "000";
signal output_signal : std_logic_vector(2 downto 0) := "000";


BEGIN


	
	process(clk,reset )
	begin

		if(reset = '1') then 
			current_index <= "0000";
			deck <= (   	"100", "001", "011", "010", "100", "010", "011", "001", "001", "011", "100", "010", "011", "001", 
						"010", "100"	
				    );
			
		elsif(rising_edge(clk)) then
		
			if(current_index = "1110") then 
				current_index <= "0000";
			else 
				temp <= deck(to_integer(unsigned(current_index)));
				deck(to_integer(unsigned(current_index))) <= deck(to_integer(unsigned(output_signal)));
				deck(to_integer(unsigned(output_signal))) <= temp;
				current_index <= current_index + 1;

			end if;
			output_signal <= deck(to_integer(unsigned(current_index)));
		end if;
	card_out <= deck(to_integer(unsigned(current_index)));
	index_out <= current_index;
	output_signal_test <= output_signal;
	
	end process;


END behavioural;

// VHDL entity CardValueP2Register, as the project stores it:
--------------------------------------------------------------------------------
-- Project :
-- File    :
-- Autor   :
-- Date    :
--
--------------------------------------------------------------------------------
-- Description :
--
--------------------------------------------------------------------------------

LIBRARY ieee;
USE ieee.std_logic_1164.all;

ENTITY CardValueP2Register IS
  PORT (
CLK: in std_logic;
  	   RESET: in std_logic;
  	   value_in : in std_logic_vector(5 downto 0);
  	   value_out: out std_logic_vector(5 downto 0)
    );
END CardValueP2Register;

--------------------------------------------------------------------------------
--Complete your VHDL description below
--------------------------------------------------------------------------------

ARCHITECTURE TypeArchitecture OF CardValueP2Register IS
signal output : std_logic_vector(5 downto 0) := "000000";


BEGIN
	process(CLK, RESET)
	begin	
		if RESET = '1' then 
			output <= "000000";
		elsif rising_edge(CLK) then 
			output <= value_in;
		end if;

	value_out <= output;
	end process;

END TypeArchitecture;

// VHDL entity AdderP2, as the project stores it:
--------------------------------------------------------------------------------
-- Project :
-- File    :
-- Autor   :
-- Date    :
--
--------------------------------------------------------------------------------
-- Description :
--
--------------------------------------------------------------------------------

LIBRARY ieee;
USE ieee.std_logic_1164.all;
use ieee.numeric_std.all;
use ieee.std_logic_unsigned.all;


ENTITY AdderP2 IS
  port(A: in std_logic_vector(5 downto 0);
  	  B: in std_logic_vector(5 downto 0);
  	  RESET: in std_logic;

  	  sum: out std_logic_vector(5 downto 0);
  	  cout: out std_logic
    );
END AdderP2;

architecture arh1 of AdderP2 is
  signal output : std_logic_vector(5 downto 0) := "000000";
  signal carryOut : std_logic := '0';

begin
  process(A, B, RESET)
    variable carry : std_logic := '0';
    variable sum : std_logic_vector(5 downto 0) := "000000";
  begin
    if RESET = '1' then
      carry := '0';
      sum := (others => '0');
    else
      for i in 0 to 5 loop
        sum(i) := A(i) xor B(i) xor carry;
        carry := (A(i) and B(i)) or (carry and (A(i) xor B(i)));
      end loop;
    end if;

    output <= sum;
    carryOut <= carry;
  end process;
  
  sum <= output;
  cout <= carryOut;
  
end arh1;

// VHDL entity ComparatorP1, as the project stores it:
--------------------------------------------------------------------------------
-- Project :
-- File    :
-- Autor   :
-- Date    :
--
--------------------------------------------------------------------------------
-- Description :
--
--------------------------------------------------------------------------------

LIBRARY ieee;
USE ieee.std_logic_1164.all;
use ieee.std_logic_unsigned.all;
use ieee.numeric_std.all;

ENTITY ComparatorP1 IS
  PORT (A: in std_logic_vector(5 downto 0);
  	   
	   Over21: out std_logic;
	   Under21: out std_logic;
	   Is21: out std_logic
    );
END ComparatorP1;

--------------------------------------------------------------------------------
--Complete your VHDL description below
--------------------------------------------------------------------------------

ARCHITECTURE TypeArchitecture OF ComparatorP1 IS

BEGIN

	Over21 <= '1' when (unsigned(A) > 21) else '0';
	Under21 <= '1' when (unsigned(A) < 21) else '0';
	Is21 <= '1' when (unsigned(A) = 21) else '0';


END TypeArchitecture;

// VHDL entity ComparatorP2, as the project stores it:
--------------------------------------------------------------------------------
-- Project :
-- File    :
-- Autor   :
-- Date    :
--
--------------------------------------------------------------------------------
-- Description :
--
--------------------------------------------------------------------------------

LIBRARY ieee;
USE ieee.std_logic_1164.all;
use ieee.std_logic_unsigned.all;
use ieee.numeric_std.all;

ENTITY ComparatorP2 IS
  PORT (
	   A: in std_logic_vector(5 downto 0);

	   Over21: out std_logic;
	   Under21: out std_logic;
	   Is21: out std_logic
    );
END ComparatorP2;

--------------------------------------------------------------------------------
--Complete your VHDL description below
--------------------------------------------------------------------------------

ARCHITECTURE TypeArchitecture OF ComparatorP2 IS
signal bust : std_logic := '0';
signal under : std_logic := '0';
signal blackjack : std_logic := '0';

BEGIN

	Over21 <= '1' when (unsigned(A) > 21) else '0';
	Under21 <= '1' when (unsigned(A) < 21) else '0';
	Is21 <= '1' when (unsigned(A) = 21) else '0';


END TypeArchitecture;

// VHDL entity UC, as the project stores it:
--------------------------------------------------------------------------------
-- Project :
-- File    :
-- Autor   :
-- Date    :
--
--------------------------------------------------------------------------------
-- Description :
-- CAND VA FI ACTIVAT ENABLE_FISHER_YATES, folosind o poarta AND se va activa clock ul la FISHER YATES RANDOM GENERATOR
--astfel generandu-se carti (daca jucatorul trage carti) 
--------------------------------------------------------------------------------

-- DE FACUT:
	--MOMENTAN DACA SE APASA STAND SI MERGE CLOCK-UL, SE EXTRAGE O CARTE INAINTE DE A SE TRECE LA URM NIVEL
	--TREBUIE FACUT CA HIT/STAND pt jucatori sa fie independent de clock/sa activeze clock-ul in functie de 
	--BUTOANELE HIT STAND CU PORTI LOGICE 

LIBRARY ieee;
USE ieee.std_logic_1164.all;
use ieee.numeric_std.all;
use ieee.std_logic_unsigned.all;

ENTITY UC IS
  PORT (START: in std_logic;
  	   CLK: in std_logic;
  	   RESET: in std_logic;
  	   restart: in std_logic;
  	   end_game: in std_logic;
  	   P1_READY: in std_logic;
  	   P2_READY: in std_logic;


  	   idle_led: out std_logic;
  	   P1_READY_LED: out std_logic;
  	   P2_READY_LED: out std_logic;
  	   game_started: out std_logic; 	--LED

  	   enable_clk : out std_logic;

  	   
  	   demux_sel_p1 : out std_logic;
  	   demux_sel_p2: out std_logic;

	   draw_p1 : out std_logic;
	   draw_p2 : out std_logic;
	   check_win : in std_logic;
	   check_bust : in std_logic; 
	   p1_cardvalue : in std_logic_vector(5 downto 0);
	   p2_cardvalue : in std_logic_vector(5 downto 0);

	   DRAW_LED : out std_logic;
	   P1_WIN : out std_logic;
	   P2_WIN : out std_logic;

	   reset_state : out std_logic;
	   restart_state: out std_logic;
	   end_game_state: out std_logic;


  	   P1_HIT: in std_logic;
  	   P1_STAND: in std_logic;
  	   P2_HIT: In std_logic;
  	   P2_STAND: in std_logic

  	   

    );
END UC;

--------------------------------------------------------------------------------
--Complete your VHDL description below
--------------------------------------------------------------------------------

ARCHITECTURE beh OF UC IS

type STARE_T is (ST0, ST1, ST2, ST3, ST4, ST5, FINAL_STATE);
signal stare, nextStare : STARE_T := ST0;

BEGIN
	Actualizare_stare: process(CLK, START)
	begin
		if rising_edge(CLK) then
			if START = '0' then stare <= ST0;	
				else stare <= nextStare;
			end if;
		end if;
		
	end process Actualizare_stare;

	Tranzitii_stari: process (START, P1_READY, P2_READY, CLK, P1_STAND, P2_STAND,P1_HIT, p2_hit,p1_cardvalue,p2_cardvalue, restart, reset, end_game)
	begin
		idle_led <= '1'; game_started <= '0'; 
		 enable_clk <= '0';
		demux_sel_p1 <= '0'; demux_sel_p2 <= '0'; draw_led <= '0'; p1_win <= '0'; p2_win <= '0';
		restart_state <= '0'; reset_state <= '0'; end_game_state <= '0';
		case stare is
			when ST0 => if START = '1' and P1_READY = '1' and P2_READY = '1' then 
				         nextStare <= ST1;
				        else nextStare <= ST0;
				        end if;
				        
			when ST1 => game_started <= '1'; idle_led <= '0';
					  enable_clk <= '1';
					  nextStare <= ST2; demux_sel_p1 <= '0';
			when ST2 => game_started <= '1'; idle_led <= '0';
					  enable_clk <= '1'; demux_sel_p2 <= '1';
					  nextStare <= ST3;

					  
			when ST3 =>  idle_led <= '0';	
				         demux_sel_p1 <= '0'; demux_sel_p2 <= '0';
					  if(check_win = '1' or check_bust = '1') then
					  	nextStare <= ST5;
				        
				       elsif(p1_stand = '1' and p1_hit = '0') then
				       	if(to_integer(unsigned(p1_cardvalue)) > 14) then
				       		nextStare <= ST4;
				       	else
				       		report "Draw more cards";
				    			nextStare <= ST3;
				    		end if;
				    	end if;
					  

			
			when ST4 => idle_led <= '0'; demux_sel_p2 <= '1'; demux_sel_p1 <= '0';
					if(check_win = '1' or check_bust = '1') then
						nextStare <= ST5;
					
					
					elsif(p2_stand = '1' and p2_hit = '0') then
						if(to_integer(unsigned(p2_cardvalue)) > 14) then
							nextStare <= ST5;
						else
							report "Draw more cards";
							nextStare <= ST4;
						end if;
					end if;
			
			when ST5 => idle_led <= '0';
			if(to_integer(unsigned(p1_cardvalue)) > 21 ) then
				P1_WIN <= '0'; P2_win <= '1'; draw_led <= '0';
			elsif(to_integer(unsigned(p2_cardvalue)) > 21) then
				P1_win <= '1'; P2_win <= '0'; draw_led <= '0';
			elsif(to_integer(unsigned(p1_cardvalue)) = 21) then
				P1_win <= '1'; P2_win <='0'; draw_led <= '0';
			elsif(to_integer(unsigned(p2_cardvalue)) = 21) then
				p2_win <= '1'; p1_win <='0'; draw_led <= '0';
			elsif(to_integer(unsigned(p1_cardvalue)) = (to_integer(unsigned(p2_cardvalue)))) then
				DRAW_LED <= '1'; P1_WIN <= '0'; P2_WIN <='0';
			elsif(to_integer(unsigned(p1_cardvalue)) > (to_integer(unsigned(p2_cardvalue)))) then
				P1_WIN <= '1'; P2_WIN <= '0'; DRAW_LED <= '0';
			else P2_WIN <= '1' ; P1_WIN <= '0'; DRAW_LED <= '0';
			end if;

			if(reset = '1') then
				reset_state <= '1'; restart_state <= '0'; end_game_state <= '0';
				nextStare <= ST1;
			elsif (restart = '1') then
				restart_state <= '1'; reset_state <= '0'; end_game_state <= '0';
				nextStare <= ST1;
			elsif (END_game = '1') then
				end_game_state <= '1'; reset_state <= '0' ; restart_state <= '0';
				nextStare <= ST0;
			end if;
			
					  
					  
			when others => idle_led <= '0';
					   
		end case;
	end process Tranzitii_stari;

	process(P1_HIT, check_win, check_bust)
	begin
	draw_p1 <= '0';
	if(stare = st3 and check_win = '0' and check_bust = '0') then
		if(p1_hit = '1' and p1_stand ='0') then 
			draw_p1 <= '1';
		end if;
	end if;


	end process;

	process(P2_HIT, check_win, check_bust)
	begin

	draw_p2 <= '0';
		
	if(stare = ST4 and check_win = '0' and check_bust = '0') then
		if(p2_hit = '1' and p2_stand = '0') then
			draw_p2 <= '1';
		end if;
	end if;
	end process;

	process(P1_READY, P2_READY)
	begin
		if(P1_READY = '1') then
			P1_READY_LED <= '1';
		else P1_READY_LED <= '0';
		end if;

		if(P2_READY = '1') then
			P2_READY_LED <= '1';
		else P2_READY_LED <= '0';
		end if;

	end process;



END beh;

// VHDL entity DecoderCardValue, as the project stores it:
--------------------------------------------------------------------------------
-- Project :
-- File    :
-- Autor   :
-- Date    :
--
--------------------------------------------------------------------------------
-- Description :
--
--------------------------------------------------------------------------------

LIBRARY ieee;
USE ieee.std_logic_1164.all;
use ieee.std_logic_unsigned.all;
use ieee.numeric_std.all;

ENTITY DecoderCardValue IS
  PORT (value_in : in std_logic_vector(5 downto 0);
  	   RESET: in std_logic;
  	   value_out: out std_logic_vector(5 downto 0);
  	   suit_out: out std_logic_vector(1 downto 0)
    );
END DecoderCardValue;

--------------------------------------------------------------------------------
--Complete your VHDL description below
--------------------------------------------------------------------------------

ARCHITECTURE TypeArchitecture OF DecoderCardValue IS
signal output : std_logic_vector(5 downto 0) := "000000";
signal output_suit : std_logic_vector(1 downto 0) := "00";

BEGIN
	process(RESET, value_in)
	begin
		if RESET = '1' then 
			output <= "000000";
		elsif RESET = '0' then
			if (to_integer(unsigned(value_in)) > 0 and to_integer(unsigned(value_in)) < 14) then 
				if( to_integer(unsigned(value_in)) = 1) then
					output <= "001011";
					output_suit <= "00";
				elsif(to_integer(unsigned(value_in)) > 1 and to_integer(unsigned(value_in)) < 11) then 
					output <= value_in;
					output_suit <= "00";
				else 
					output <= "001010";
					output_suit <= "00";
				end if;
		
			elsif(to_integer(unsigned(value_in)) > 13 and to_integer(unsigned(value_in)) < 27) then
				if(to_integer(unsigned(value_in)) = 14) then 
					output <= "001011";	-- ACE
					output_suit <= "01";
				elsif(to_integer(unsigned(value_in)) > 14 and to_integer(unsigned(value_in)) < 24) then 
					output <= value_in - 13;
					output_suit <= "01";
				else 
					output <= "001010";
					output_suit <= "01";
				end if ;

			elsif(to_integer(unsigned(value_in)) > 26 and to_integer(unsigned(value_in)) < 40) then 
				if(to_integer(unsigned(value_in)) = 27) then	
					output <= "001011";
					output_suit <= "10";
				elsif(to_integer(unsigned(value_in)) > 27 and to_integer(unsigned(value_in)) < 37) then
					output <= value_in - 26;
					output_suit <= "10";
				else 
					output <= "001010";
					output_suit <= "10";
				end if;
			elsif(to_integer(unsigned(value_in)) > 39 and to_integer(unsigned(value_in)) < 53) then 
				if ( to_integer(unsigned(value_in)) = 40) then
					output <= "001011";
					output_suit <= "11";
				elsif(to_integer(unsigned(value_in)) > 40 and to_integer(unsigned(value_in)) < 49) then 
					output <= value_in - 39;
					output_suit <= "11";
				else 
					output <= "001010";
					output_suit <= "11";
				end if;
			else output<= "111111";
				output_suit <= "11";	--ERROR 

				

				
			end if;
		
				
		end if;
		



	end process;
	value_out <= output;
	suit_out <= output_suit;
	-- vom avea in pachet numere de la 1 la 52 
	--fiecare numar va fi o carte specifica, exact ca un pachet intreg de BJ
	-- DE la 1-13 un suit, de la 14-26 alt suit, 27->39, 40->52 
	--1 va fi AS DE HEARTS, 2-10 valoare de HEARTS, 11-13 jack queen king IN ACEASTA ORDINE DE HEARTS
	--acceeasi ordine pt urmatoarele suit-uri 
	--14 = AS DE DIAMONDS, .......  si tot asa 
	


END TypeArchitecture;

// VHDL entity and_gate, as the project stores it:
--------------------------------------------------------------------------------
-- Project :
-- File    :
-- Autor   :
-- Date    :
--
--------------------------------------------------------------------------------
-- Description :
--
--------------------------------------------------------------------------------

LIBRARY ieee;
USE ieee.std_logic_1164.all;

ENTITY and_gate IS
  PORT (A,B : in std_logic;
  	   output: out std_logic
    );
END and_gate;

--------------------------------------------------------------------------------
--Complete your VHDL description below
--------------------------------------------------------------------------------

ARCHITECTURE structural OF and_gate IS

BEGIN
	output <= A and B;


END structural;

// VHDL entity BCDto7LEFT, as the project stores it:
--------------------------------------------------------------------------------
-- Project :
-- File    :
-- Autor   :
-- Date    :
--
--------------------------------------------------------------------------------
-- Description :
--
--------------------------------------------------------------------------------

LIBRARY ieee;
USE ieee.std_logic_1164.all;
use ieee.numeric_std.all;
use ieee.std_logic_unsigned.all;

ENTITY BCDto7LEFT IS
  PORT (A: in std_logic_vector(5 downto 0);
        output : out std_logic_vector(6 downto 0)
    );
END BCDto7LEFT;

--------------------------------------------------------------------------------
--Complete your VHDL description below
--------------------------------------------------------------------------------

ARCHITECTURE TypeArchitecture OF BCDto7LEFT IS
signal out_sig : std_logic_vector(6 downto 0) := "0000000";

BEGIN
	process(A)
	begin
	if(to_integer(unsigned(A)) > 1 and to_integer(unsigned(A)) < 10) then
		out_sig <= "1111110";
	elsif(to_integer(unsigned(A)) = 10) then
		out_sig <= "0000110";
	elsif(to_integer(unsigned(A)) > 10 and to_integer(unsigned(A)) < 20) then
		out_sig <= "0000110";
	elsif(to_integer(unsigned(A)) >19 and to_integer(unsigned(A)) < 30) then
		out_sig <= "1101101";
	elsif(to_integer(unsigned(A)) > 29) then
		out_sig <= "1111001";
	else out_sig <= "1111110";
	end if;


	end process;
	output <= out_sig;	

END TypeArchitecture;

// VHDL entity BcdTo7RIGHT, as the project stores it:
--------------------------------------------------------------------------------
-- Project :
-- File    :
-- Autor   :
-- Date    :
--
--------------------------------------------------------------------------------
-- Description :
--
--------------------------------------------------------------------------------

LIBRARY ieee;
USE ieee.std_logic_1164.all;
use ieee.numeric_std.all;
use ieee.std_logic_unsigned.all;

ENTITY BcdTo7RIGHT IS
  PORT (A: in std_logic_vector(5 downto 0);
  	   output : out std_logic_vector(6 downto 0)
    );
END BcdTo7RIGHT;

--------------------------------------------------------------------------------
--Complete your VHDL description below
--------------------------------------------------------------------------------

ARCHITECTURE TypeArchitecture OF BcdTo7RIGHT IS
signal sig : std_logic_vector(6 downto 0) := "0000000";

BEGIN
	process(A)
	begin								--        		_
		case A is 				
		
		
		
		--|_|	


				
			when "000010" => sig <= "1101101";			  	  

			
			when "000011" => sig <= "1111001";
			when "000100" => sig <= "0010011";
			when "000101" => sig <= "1011011";
			when "000110" => sig <= "0011111";		
			when "000111" => sig <= "1110000";
			when "001000" => sig <= "1111111";
			when "001001" => sig <= "1111011";	
			when "001010" => sig <= "1111110";	--10 
			when "001011" => sig <= "0000110";

			when "001100" => sig <= "1101101";
			when "001101" => sig <= "1111001";
			when "001110" => sig <= "0010011";
			when "001111" => sig <= "1011011";
			when "010000" => sig <= "0011111";
			when "010001" => sig <= "1110000";
			when "010010" => sig <= "1111111";
			when "010011" => sig <= "1111011";
			when "010100" => sig <= "1111110";
			when "010101" => sig <= "0000110";	--21

			when "010110" => sig <= "1101101";
			when "010111" => sig <= "1111001";
			when "011000" => sig <= "0010011";
			when "011001" => sig <="1011011";
			when "011010" => sig <= "0011111";
			when "011011" => sig <= "1110000";
			when "011100" => sig <= "1111111";
			when "011101" => sig <= "1111011";
			when "011110" => sig <= "1111110";
			
			when others => sig <= "1111110";			
		end case;
	end process;
	output <= sig;


END TypeArchitecture;

// VHDL entity bcdto7_left_draw, as the project stores it:
--------------------------------------------------------------------------------
-- Project :
-- File    :
-- Autor   :
-- Date    :
--
--------------------------------------------------------------------------------
-- Description :
--
--------------------------------------------------------------------------------

LIBRARY ieee;
USE ieee.std_logic_1164.all;
use ieee.std_logic_unsigned.all;
use ieee.numeric_std.all;

ENTITY bcdto7_left_draw IS
  PORT (A: in std_logic_vector(5 downto 0);
  	   output : out std_logic_vector(6 downto 0)
    );
END bcdto7_left_draw;

--------------------------------------------------------------------------------
--Complete your VHDL description below
--------------------------------------------------------------------------------

ARCHITECTURE TypeArchitecture OF bcdto7_left_draw IS
signal sig : std_logic_vector(6 downto 0) := "0000000";

BEGIN
	process(A)
	begin
		if(to_integer(unsigned(A)) > 1 and to_integer(unsigned(A)) < 10) then
			sig <= "1111110";
		elsif(to_integer(unsigned(A)) > 9 and to_integer(unsigned(A)) < 11) then  
			sig <= "0000110";
		else sig <= "1111110";
		end if;


	end process;
	output <= sig;

END TypeArchitecture;

// VHDL entity bcdto7_right_draw, as the project stores it:
--------------------------------------------------------------------------------
-- Project :
-- File    :
-- Autor   :
-- Date    :
--
--------------------------------------------------------------------------------
-- Description :
--
--------------------------------------------------------------------------------

LIBRARY ieee;
USE ieee.std_logic_1164.all;
use ieee.std_logic_unsigned.all;
use ieee.numeric_std.all;

ENTITY bcdto7_right_draw IS
  PORT (A: in std_logic_vector(5 downto 0);
  	   output: out std_logic_vector(6 downto 0)
    );
END bcdto7_right_draw;

--------------------------------------------------------------------------------
--Complete your VHDL description below
--------------------------------------------------------------------------------

ARCHITECTURE TypeArchitecture OF bcdto7_right_draw IS
signal sig : std_logic_vector(6 downto 0) := "0000000";

BEGIN
	process(A)
	begin
		case A is 
			when "000010" => sig <= "1101101";			  	  

			
			when "000011" => sig <= "1111001";
			when "000100" => sig <= "0010011";
			when "000101" => sig <= "1011011";
			when "000110" => sig <= "0011111";		
			when "000111" => sig <= "1110000";
			when "001000" => sig <= "1111111";
			when "001001" => sig <= "1111011";	
			when "001010" => sig <= "1111110";	--10 
			when "001011" => sig <= "0000110";
			when others => sig <= "1111110";
			end case;
	end process;

	output <= sig;
END TypeArchitecture;

// VHDL entity and_gate_6bits, as the project stores it:
--------------------------------------------------------------------------------
-- Project :
-- File    :
-- Autor   :
-- Date    :
--
--------------------------------------------------------------------------------
-- Description :
--
--------------------------------------------------------------------------------

LIBRARY ieee;
USE ieee.std_logic_1164.all;

ENTITY and_gate_6bits IS
  PORT (A: in std_logic_vector(5 downto 0);
        B: in std_logic;
        output: out std_logic_vector(5 downto 0)
    );
END and_gate_6bits;

--------------------------------------------------------------------------------
--Complete your VHDL description below
--------------------------------------------------------------------------------

ARCHITECTURE TypeArchitecture OF and_gate_6bits IS
signal sig : std_logic_vector(5 downto 0) := "000000";

BEGIN
	process(A,B)
	begin
		if(B = '1') then
			sig <= A;
		else sig <= "000000";
		end if;
	end process;
	output <= sig;


END TypeArchitecture;

// VHDL entity SuitLed, as the project stores it:
--------------------------------------------------------------------------------
-- Project :
-- File    :
-- Autor   :
-- Date    :
--
--------------------------------------------------------------------------------
-- Description :
--
--------------------------------------------------------------------------------

LIBRARY ieee;
USE ieee.std_logic_1164.all;

ENTITY SuitLed IS
  PORT (A: in std_logic_vector(1 downto 0);
  	  enable: in std_logic;
        Hearts: out std_logic;
        Diamonds: out std_logic;
        Clubs: out std_logic;
        Spades: out std_logic
    );
END SuitLed;

--------------------------------------------------------------------------------
--Complete your VHDL description below
--------------------------------------------------------------------------------

ARCHITECTURE TypeArchitecture OF SuitLed IS

BEGIN
	Hearts <= '1' when (A = "00" and enable = '1') else '0';
	Diamonds <= '1' when (A = "01" and enable = '1') else '0';
	Clubs <= '1' when (A = "10" and enable = '1') else '0';
	Spades <= '1' when (A = "11" and enable = '1') else '0';


END TypeArchitecture;

// VHDL entity or_gate, as the project stores it:
--------------------------------------------------------------------------------
-- Project :
-- File    :
-- Autor   :
-- Date    :
--
--------------------------------------------------------------------------------
-- Description :
--
--------------------------------------------------------------------------------

LIBRARY ieee;
USE ieee.std_logic_1164.all;

ENTITY or_gate IS
  PORT (A,B: in std_logic;
  	   output : out std_logic
    );
END or_gate;

--------------------------------------------------------------------------------
--Complete your VHDL description below
--------------------------------------------------------------------------------

ARCHITECTURE TypeArchitecture OF or_gate IS
signal out_sig : std_logic := '0';

BEGIN
	process(A,B)
	begin
		if(A = '1' or B = '1') then
			out_sig <= '1';
		else out_sig <= '0';
		end if;

	end process;
	output <= out_sig;


END TypeArchitecture;

// VHDL entity xor_gate, as the project stores it:
--------------------------------------------------------------------------------
-- Project :
-- File    :
-- Autor   :
-- Date    :
--
--------------------------------------------------------------------------------
-- Description :
--
--------------------------------------------------------------------------------

LIBRARY ieee;
USE ieee.std_logic_1164.all;

ENTITY xor_gate IS
  PORT (A,B : in std_logic;
  	   output : out std_logic
    );
END xor_gate;

--------------------------------------------------------------------------------
--Complete your VHDL description below
--------------------------------------------------------------------------------

ARCHITECTURE TypeArchitecture OF xor_gate IS

BEGIN
	output <= A XOR B;


END TypeArchitecture;

// VHDL entity demux1to2, as the project stores it:
--------------------------------------------------------------------------------
-- Project :
-- File    :
-- Autor   :
-- Date    :
--
--------------------------------------------------------------------------------
-- Description :
--
--------------------------------------------------------------------------------

LIBRARY ieee;
USE ieee.std_logic_1164.all;

ENTITY demux1to2 IS
  PORT (data_in : in std_logic;
        Select_data: in std_logic;
        I0,I1 : out std_logic
    );
END demux1to2;

--------------------------------------------------------------------------------
--Complete your VHDL description below
--------------------------------------------------------------------------------

ARCHITECTURE TypeArchitecture OF demux1to2 IS
signal i1_sig, i2_sig : std_logic := '0';

BEGIN
	process(data_in, select_data)
	begin
		if(select_data = '0') then
			if(data_in = '0') then
				i1_sig <= '0';
				i2_sig <= '0';
			else 
				i1_sig <= '1';
				i2_sig <= '0';
			end if;
		elsif(select_data = '1') then
			if(data_in = '0') then
				i1_sig <= '0';
				i2_sig <= '0';
			else 
				i1_sig <= '0';
				i2_sig <= '1';
			end if;
		end if;


	end process;
	I0 <= i1_sig;
	I1 <= i2_sig;


END TypeArchitecture;

// VHDL entity ScoreCounter, as the project stores it:
--------------------------------------------------------------------------------
-- Project :
-- File    :
-- Autor   :
-- Date    :
--
--------------------------------------------------------------------------------
-- Description :
--
--------------------------------------------------------------------------------

LIBRARY ieee;
USE ieee.std_logic_1164.all;
use ieee.numeric_std.all;
use ieee.std_logic_unsigned.all;

ENTITY ScoreCounter IS
  PORT (CLK : in std_logic;
  	   RESET: in std_logic;
  	   output : out std_logic_vector(5 downto 0)
  	   
    );
END ScoreCounter;

--------------------------------------------------------------------------------
--Complete your VHDL description below
--------------------------------------------------------------------------------

ARCHITECTURE TypeArchitecture OF ScoreCounter IS
signal count : std_logic_vector(5 downto 0) := "000000";

BEGIN
	process(CLK)
	begin
		if(rising_edge(CLK)) then
			count <= count + 1;
		
		end if;
	end process;
	output <= count;


END TypeArchitecture;
